# Fritzing sketch cloudScaleSchematic (saved by Fritzing 0.8.5b)

parts:
  U1 = LIPO-110mAh [package=lipo-110]
  BAT1 = Battery Holders [package=battcom_20mm_pth]
  LCD1 = LCD screen
  Part3 = Arduino Pro Mini v13
  U4 = ESP8266 WiFi Module [part_number=ESP8266]
  Part4 = Power Cell LiPo Charger/Booster

nets:
  N1: U1.+, Part4.VBATT
  GND: U1.-, BAT1.-, LCD1.V0, Part3.GND, U4.GND, Part4.GND
  N2: BAT1.+, LCD1.VDD
  N3: LCD1.E, Part4.EN
  N4: LCD1.DB2, Part3.A5
  N5: LCD1.DB3, Part3.A4
  N6: LCD1.DB4, Part3.A3
  N7: LCD1.DB5, Part3.A2
  N8: LCD1.DB6, Part3.A1
  N9: LCD1.DB7, Part3.A0
  VCC: Part3.VCC, U4.VCC, U4.CH_PD, Part4.VCC
  N10: Part3.D6_PWM, U4.RST
  N11: Part3.D5_PWM, U4.GPIO_0
  N12: Part3.D3_PWM, U4.TXD
  N13: Part3.D2, U4.RXD

custom parts:
  ESP8266 WiFi Module: Generic WiFi Module based on the ESP8266 with onboard PCB antenna and UART communications
